# Fritzing sketch menù schema (saved by Fritzing 0.9.3b)
breadboards: 1

parts:
  Arduino = Arduino Uno (Rev3)
  LCD1 = LCD screen
  R1 = Resistor [tolerance=±5% resistance=220 package=THT]
  S1 = Pushbutton [package="[THT]"]
  S2 = Pushbutton [package="[THT]"]
  S3 = Pushbutton [package="[THT]"]
  R2 = Resistor [tolerance=±5% resistance=10k package=THT]
  R3 = Resistor [tolerance=±5% resistance=10k package=THT]
  R5 = Resistor [tolerance=±5% resistance=100 package=THT]
  R6 = Resistor [tolerance=±5% resistance=220 package=THT]
  DHT1 = DHT11 Humitidy and Temperature Sensor
  R4 = Resistor [tolerance=±5% resistance=10k package=THT]

nets:
  N1: Arduino.A2, S1.Pin_1, S1.Pin_2, R2.Pin_1
  N2: Arduino.A3, S3.Pin_1, S3.Pin_2, R3.Pin_1
  N3: Arduino.A4/SDA, S2.Pin_1, S2.Pin_2, R4.Pin_1
  N4: Arduino.D8, DHT1.DATA
  N5: Arduino.D2, LCD1.RS
  N6: Arduino.D3_PWM, LCD1.E
  N7: Arduino.D4, LCD1.DB4
  N8: Arduino.D5_PWM, LCD1.DB5
  N9: Arduino.D6_PWM, LCD1.DB6
  N10: Arduino.D7, LCD1.DB7
  VDD: Arduino.5V, LCD1.VDD, R1.Pin_0, S1.Pin_3, S1.Pin_4, S2.Pin_3, S2.Pin_4, S3.Pin_3, S3.Pin_4, R6.Pin_0, DHT1.VDD
  GND: Arduino.GND, LCD1.VSS, LCD1.R/W, LCD1.LED-, R2.Pin_0, R3.Pin_0, R5.Pin_0, DHT1.GND, R4.Pin_0
  N11: LCD1.V0, R5.Pin_1, R6.Pin_1
  N12: LCD1.LED+, R1.Pin_1

custom parts:
  DHT11 Humitidy and Temperature Sensor: DHT11 Humidity and Temperature Sensor

// code stored in the sketch: 1_Termostato.ino
void Termostato(){
  if(c==0){
    lcd.clear();
    lcd.setCursor(0, 0);
    lcd.print("T=");
    lcd.setCursor(5, 0);
    lcd.print("U=");
    lcd.setCursor(0, 1);
    lcd.print("* Esci");
  }
  c=c+1;
  delay(10);
  if(digitalRead(A3)==HIGH){
    enter=1-enter;
    delay(1000);
    ca=0;
    cb=0;
  }
  int t=dht.readTemperature();
  int h=dht.readHumidity();
  lcd.setCursor(2, 0);
  lcd.print(t);
  lcd.setCursor(7, 0);
  lcd.print(h);
  lcd.setCursor(0,1);
  lcd.blink();
}

// code stored in the sketch: 2_Opzione2.ino
void Opzione2(){
  if(c==0){
    lcd.clear();
  }
  c=c+1;
  if(digitalRead(A3)==HIGH){
    enter=1-enter;
    delay(1000);
    ca=0;
    cb=0;
  }
  lcd.setCursor(0,0);
  lcd.print("Error->no comand");
  lcd.setCursor(0, 1);
  lcd.print("* Esci");
  lcd.setCursor(0,1);
  lcd.blink();
  delay(10);
}

// code stored in the sketch: 3_Opzione3.ino
void Opzione3(){
  if(c==0){
    lcd.clear();
  }
  c=c+1;
  if(digitalRead(A3)==HIGH){
    enter=1-enter;
    delay(1000);
    ca=0;
    cb=0;
  }
  lcd.setCursor(0,0);
  lcd.print("Error->no comand");
  lcd.setCursor(0, 1);
  lcd.print("* Esci");
  lcd.setCursor(0,1);
  lcd.blink();
  delay(10);
}

// code stored in the sketch: 4_Impostazioni.ino
void Impostazioni(){
  char cau=0;
  if(c==0){
    ca=0;
    cb=0;
    lcd.clear();
    lcd.setCursor(0,0);
    lcd.print("* V.anim.");
    lcd.setCursor(0, 1);
    lcd.print("* Esci");
  }
  c=c+1;
  if(digitalRead(A2)==HIGH){
    cb=1-cb;
    cc=cc+1;
    delay(500);
  }
  if(digitalRead(A4)==HIGH){
    cb=1-cb;
    cc=cc-1;
    delay(500);
  }
  if(digitalRead(A3)==HIGH){
    cau=1-cau;
    delay(500);
  }
  delay(10);
  if(cc>1){
    cc=0;
  }
  while(cau==1 && cc==0){
    if(pausa<100){
    lcd.setCursor(13,0);
    lcd.print("  ");
    }
    if(pausa>995){
      pausa=0;
    }
    lcd.setCursor(11,0);
    lcd.print(pausa);
    lcd.setCursor(10,0);
    lcd.blink();
    if(digitalRead(A3)==HIGH){
      cau=0;
      delay(500);
    }
    if(digitalRead(A2)==HIGH){
      pausa=pausa+5;
      lcd.setCursor(2,0);
      lcd.print("         ");
      delay(pausa);
      lcd.setCursor(2,0);
      lcd.print("V");
      delay(pausa);
      lcd.print(".");
      delay(pausa);
      lcd.print("a");
      delay(pausa);
      lcd.print("n");
      delay(pausa);
      lcd.print("i");
      delay(pausa);
      lcd.print("m");
      delay(pausa);
      lcd.print(".");
      delay(pausa);
    }
    if(digitalRead(A4)==HIGH){
      pausa=pausa-5;
      lcd.setCursor(2,0);
      lcd.print("         ");
      delay(pausa);
      lcd.setCursor(2,0);
      lcd.print("V");
      delay(pausa);
      lcd.print(".");
      delay(pausa);
      lcd.print("a");
      delay(pausa);
      lcd.print("n");
      delay(pausa);
      lcd.print("i");
      delay(pausa);
      lcd.print("m");
      delay(pausa);
      lcd.print(".");
      delay(pausa);
    }
  }
  lcd.setCursor(11,0);
  lcd.print("    ");
  lcd.setCursor(11,0);
  lcd.print(pausa);
  lcd.setCursor(0,cc);
  lcd.blink();
  if(digitalRead(A3)==HIGH && cc==1){
    enter=0;
    delay(500);
  }
}

// code stored in the sketch: First_boot.ino
void bootanimation(){
  lcd.print("P");
  delay(100);
  lcd.print("r");
  delay(100);
  lcd.print("o");
  delay(100);
  lcd.print("j");
  delay(100);
  lcd.print("e");
  delay(100);
  lcd.print("c");
  delay(100);
  lcd.print("t");
  delay(100);
  lcd.setCursor(0,1);
  lcd.print("F");
  delay(100);
  lcd.print("i");
  delay(100);
  lcd.print("t");
  delay(100);
  lcd.print("z");
  delay(100);
  lcd.print("g");
  delay(100);
  lcd.print("e");
  delay(100);
  lcd.print("r");
  delay(100);
  lcd.print("a");
  delay(100);
  lcd.print("l");
  delay(100);
  lcd.print("d");

  
  delay(500);
  lcd.setCursor(11, 1);
  lcd.print("EX");
  delay(500);
  lcd.setCursor(11,1);
  lcd.print("  ");
  delay(500);
  lcd.setCursor(11, 1);
  lcd.print("EX");
  delay(500);
  lcd.setCursor(11,1);
  lcd.print("  ");
  delay(500);
  lcd.setCursor(11, 1);
  lcd.print("EX");
  delay(500);
  lcd.setCursor(11,1);
  lcd.print("  ");
  delay(500);
  lcd.setCursor(11, 1);
  lcd.print("EX");
  delay(3000);
  lcd.setCursor(12,1);
  lcd.print(" ");
  delay(100);
  lcd.setCursor(11,1);
  lcd.print(" ");
  delay(100);
  lcd.setCursor(9, 1);
  lcd.print(" ");
  delay(100);
  lcd.setCursor(8, 1);
  lcd.print(" ");
  delay(100);
  lcd.setCursor(7, 1);
  lcd.print(" ");
  delay(100);
  lcd.setCursor(6, 1);
  lcd.print(" ");
  delay(100);
  lcd.setCursor(5, 1);
  lcd.print(" ");
  delay(100);
  lcd.setCursor(4, 1);
  lcd.print(" ");
  delay(100);
  lcd.setCursor(3, 1);
  lcd.print(" ");
  delay(100);
  lcd.setCursor(2, 1);
  lcd.print(" ");
  delay(100);
  lcd.setCursor(1, 1);
  lcd.print(" ");
  delay(100);
  lcd.setCursor(0, 1);
  lcd.print(" ");
  delay(100);
  lcd.setCursor(6, 0);
  lcd.print(" ");
  delay(100);
  lcd.setCursor(5, 0);
  lcd.print(" ");
  delay(100);
  lcd.setCursor(4, 0);
  lcd.print(" ");
  delay(100);
  lcd.setCursor(3, 0);
  lcd.print(" ");
  delay(100);
  lcd.setCursor(2, 0);
  lcd.print(" ");
  delay(100);
  lcd.setCursor(1, 0);
  lcd.print(" ");
  delay(100);
  lcd.setCursor(0, 0);
  lcd.print(" ");
  delay(100);
}

// code stored in the sketch: Menu_beta.ino
/*
 * MENU ARDUINO - v 0.1-2 Alpha
 * 
 * CHANGELOG:
 * * 0.1-1 ** Alpha ** 01:55  03/01/2019 ** First Release
 * / Diario del programmatore, data astrale 3119.1, ho sviluppato la prima 
 *  versione utilizzabile(ma non troppo) del programma e dispositivo, ho riscontrato un bug
 *  nell'unica opzione di Termostato, vista la stanchezza e la frequente abitudine delle
 *  mie palpebre nell'abbassarsi temo che non potrò risolvere i problemi nell'immediato arco di
 *  tempo e sono obbligato ad andare a dormire e posporre il compito a un'altro periodo utile. Di
 *  seguito elenco il primo changelog relativo a questa versione. \
 *  
 *  - Menù con animazioni
 *  - Bootanimation v 1
 *  - Termostato
 *  - Controllo tramite pulsanti
 * 
 * / Diario del programmatore, complemento, ieri sera mi sono dimenticato di aggiungere i bug, vista
 * la stanchezza non me ne sorprendo, li elenco qui di seguito. \
 * 
 * [BUG] il termostato non si chiude, se si tenta di uscire il cursore va al punto (0,0) dell' LCD
 * 
 * ******************************************************************************************************
 * 
 * * 0.1-2 ** Alpha ** 12:48 03/01/2019 ** Bugfix
 * / Diario del programmatore, data astrale 3119.12, ho effettuato delle correzione del codice e lo
 *  ho ottimizzato, sto per aggiungere le impostazioni del dispositivo che permetteranno di controllare
 *  le animazioni, di seguito elenco le novità di questa versione. \
 *  
 *  - Risolto il problema del termostato
 *  - Ottimizzazione del codice
 *  
 *  *****************************************************************************************************
 * 
 * * 0.2-1 ** Alpha ** 21:15 02/01/2019 ** Update
 * / Diario del programmatore, data astrale 3119.21, ho sviluppato una seconda versione Alpha del
 *  dispositivo in cui ho aggiunto la sezione impostazioni in cui è possibile modificare la velocità delle
 *  animazioni(temporaneamente solo in versione avanzata). \
 *  
 *  - Aggiunta la sezione "Impostazioni"
 *  - Controllo delle animazioni da parte dell'utilizzatore
 *  
*/
#include <DHT.h>
#include <LiquidCrystal.h>
#define DHTPIN 8  
#define DHTTYPE DHT11
DHT dht(DHTPIN, DHTTYPE);
const char rs = 2, en = 3, d4 = 4, d5 = 5, d6 = 6, d7 = 7;
LiquidCrystal lcd(rs, en, d4, d5, d6, d7);
char cursore=0;
bool down=0;
bool enter=0;
bool up=0;
bool cm=0;
signed int c;
signed int ca;
signed int cb;
signed int cc;
int pausa=100;

void setup(){
  pinMode(A2, INPUT);
  pinMode(A3, INPUT);
  pinMode(A4, INPUT);
  lcd.begin(16,2);
  bootanimation();
}

void loop(){
  if(cursore==0 || cursore==1){
    if(ca==0){
      lcd.noBlink();
      lcd.clear();
      lcd.print("*");
      lcd.setCursor(0,1);
      lcd.print("*");
      delay(pausa);
      lcd.setCursor(1,0);
      lcd.print(" ");
      lcd.setCursor(1,1);
      lcd.print(" ");
      delay(pausa);
      lcd.setCursor(2,0);
      lcd.print("T");
      lcd.setCursor(2,1);
      lcd.print("O");
      delay(pausa);
      lcd.setCursor(3,0);
      lcd.print("e");
      lcd.setCursor(3,1);
      lcd.print("p");
      delay(pausa);
      lcd.setCursor(4,0);
      lcd.print("r");
      lcd.setCursor(4,1);
      lcd.print("z");
      delay(pausa);
      lcd.setCursor(5,0);
      lcd.print("m");
      lcd.setCursor(5,1);
      lcd.print("i");
      delay(pausa);
      lcd.setCursor(6,0);
      lcd.print("o");
      lcd.setCursor(6,1);
      lcd.print("o");
      delay(pausa);
      lcd.setCursor(7,0);
      lcd.print("s");
      lcd.setCursor(7,1);
      lcd.print("n");
      delay(pausa);
      lcd.setCursor(8,0);
      lcd.print("t");
      lcd.setCursor(8,1);
      lcd.print("e");
      delay(pausa);
      lcd.setCursor(9,0);
      lcd.print("a");
      lcd.setCursor(9,1);
      lcd.print("2");
      delay(pausa);
      lcd.setCursor(10,0);
      lcd.print("t");
      delay(pausa);
      lcd.setCursor(11,0);
      lcd.print("o");
      delay(pausa);
      lcd.setCursor(14, 0);
      lcd.print("P1");
    }
    ca=ca+1;
    lcd.setCursor(0, cm);
    lcd.blink();
    cb=0;
  }
  if(cursore==2 || cursore==3){
    if(cb==0){
      lcd.noBlink();
      lcd.clear();
      lcd.print("*");
      lcd.setCursor(0,1);
      lcd.print("*");
      delay(pausa);
      lcd.setCursor(1,0);
      lcd.print(" ");
      lcd.setCursor(1,1);
      lcd.print(" ");
      delay(pausa);
      lcd.setCursor(2,0);
      lcd.print("O");
      lcd.setCursor(2,1);
      lcd.print("I");
      delay(pausa);
      lcd.setCursor(3,0);
      lcd.print("p");
      lcd.setCursor(3,1);
      lcd.print("m");
      delay(pausa);
      lcd.setCursor(4,0);
      lcd.print("z");
      lcd.setCursor(4,1);
      lcd.print("p");
      delay(pausa);
      lcd.setCursor(5,0);
      lcd.print("i");
      lcd.setCursor(5,1);
      lcd.print("o");
      delay(pausa);
      lcd.setCursor(6,0);
      lcd.print("o");
      lcd.setCursor(6,1);
      lcd.print("s");
      delay(pausa);
      lcd.setCursor(7,0);
      lcd.print("n");
      lcd.setCursor(7,1);
      lcd.print("t");
      delay(pausa);
      lcd.setCursor(8,0);
      lcd.print("e");
      lcd.setCursor(8,1);
      lcd.print("a");
      delay(pausa);
      lcd.setCursor(9,0);
      lcd.print("3");
      lcd.setCursor(9,1);
      lcd.print("z");
      delay(pausa);
      lcd.setCursor(10,1);
      lcd.print("i");
      delay(pausa);
      lcd.setCursor(11,1);
      lcd.print("o");
      delay(pausa);
      lcd.setCursor(12,1);
      lcd.print("n");
      delay(pausa);
      lcd.setCursor(13,1);
      lcd.print("i");
      delay(pausa);
      lcd.setCursor(14, 0);
      lcd.print("P2");
    }
    cb=cb+1;
    lcd.setCursor(0, cm);
    lcd.blink();
    ca=0;
  }
  if(digitalRead(A2)==HIGH){
    down=1-down;
    cm=1-cm;
    cursore=cursore+1;
    delay(500);
  }
  if(digitalRead(A3)==HIGH){
    enter=1-enter;
    delay(500);
  }
  if(digitalRead(A4)==HIGH){
    up=1-up;
    cm=1-cm;
    cursore=cursore-1;
    delay(500);
  }
  while(enter==1 && cursore==0){
    Termostato();
  }
  while(enter==1 && cursore==1){
    Opzione2();
  }
  while(enter==1 && cursore==2){
    Opzione3();
  }
  while(enter==1 && cursore==3){
    Impostazioni();
  }
  if(cursore>3){
    cursore=0;
    lcd.setCursor(0,0);
    lcd.blink();
  }
  if(cursore<0){
    cursore=3;
    lcd.setCursor(0,1);
    lcd.blink();
  }
  c=0;
  delay(10);
}
